# Fritzing sketch skematik_rangkaian (saved by Fritzing 0.9.3b)
breadboards: 1

parts:
  Part2 = RFID-RC522-v2
  LED2 = LED - 5mm [color="Yellow (595nm)" package="5 mm [THT]"]
  LED3 = LED - 5mm [color="Green (560nm)" package="5 mm [THT]"]
  Part5 = Arduino Mega 2560 (Rev3)
  LCD1 = LCD screen
  LCM1602_IIC3 = LCM1602 IIC [part_number="LCM1602 IIC" chip_label="LCM1602 IIC" package="DIP (Dual Inline) [THT]"]
  R1 = Resistor [tolerance=±5% resistance=220 package="0402 [SMD]"]
  R2 = Resistor [tolerance=±5% resistance=220 package="0402 [SMD]"]
  R3 = Resistor [tolerance=±5% resistance=220 package="0402 [SMD]"]
  LED1 = smd LED [color="Red (633nm)" package="0603 [SMD]"]
  J2 = Piezo Speaker
  Part7 = MicroSD Card Module
  ZS-042_RTC1 = ZS-042 RTC Module
  J1 = Basic Servo
  VCC1 = Battery block 9V  # not connected

nets:
  N1: Part2.SDA, Part5.D53
  N2: Part2.SCK, Part5.D52, Part7.SCK
  N3: Part2.MOSI, Part5.D51, Part7.MOSI
  N4: Part2.MISO, Part5.D50, Part7.MISO
  GND: Part2.GND, LED2.cathode, LED3.cathode, Part5.GND, LCM1602_IIC3.GND, LED1.cathode, J2.pin1, Part7.GND, ZS-042_RTC1.GND, J1.gnd
  N5: Part2.RST, Part5.D5_PWM
  3.3V: Part2.3.3V, Part5.3V3
  N6: LED2.anode, R1.Pin_1
  N7: LED3.anode, R3.Pin_0
  N8: Part5.D21/SCL, Part5.SCL, LCM1602_IIC3.SCL, ZS-042_RTC1.SCL
  N9: Part5.D20/SDA, Part5.SDA, LCM1602_IIC3.SDA, ZS-042_RTC1.SDA
  VCC: Part5.5V, LCM1602_IIC3.VCC, Part7.VCC, ZS-042_RTC1.VCC, J1.vcc
  N10: Part5.D4_PWM, Part7.CS
  N11: Part5.D6_PWM, J1.pulse
  N12: Part5.D7_PWM, J2.pin2
  N13: Part5.D40, R1.Pin_0
  N14: Part5.D41, R3.Pin_1
  N15: Part5.D42, R2.Pin_0
  VSS: LCD1.VSS, LCM1602_IIC3.VSS
  VDD: LCD1.VDD, LCM1602_IIC3.VDD
  N16: LCD1.V0, LCM1602_IIC3.V0
  N17: LCD1.RS, LCM1602_IIC3.RS
  N18: LCD1.R/W, LCM1602_IIC3.RW
  N19: LCD1.E, LCM1602_IIC3.E
  N20: LCD1.DB0, LCM1602_IIC3.D0
  N21: LCD1.DB1, LCM1602_IIC3.D1
  N22: LCD1.DB2, LCM1602_IIC3.D2
  N23: LCD1.DB3, LCM1602_IIC3.D3
  N24: LCD1.DB4, LCM1602_IIC3.D4
  N25: LCD1.DB5, LCM1602_IIC3.D5
  N26: LCD1.DB6, LCM1602_IIC3.D6
  N27: LCD1.DB7, LCM1602_IIC3.D7
  N28: LCD1.LED+, LCM1602_IIC3.A
  N29: LCD1.LED-, LCM1602_IIC3.K
  N30: LCM1602_IIC3.LED_A, LCM1602_IIC3.LED_B
  N31: R2.Pin_1, LED1.anode

custom parts:
  RFID-RC522-v2: A simple China made RFID-RC522 Reader; do check the pin labels, as this is a MFRC522 based clone.
  LCM1602 IIC: I2C-Module to use a 1602 or 2004 LCD on with the wire.h libory Serial LCD Modul
